// Logisim project parte1_cache.circ as structural Verilog: 1 circuit, main circuit main
module main (
  input  [5:0] Endereco,
  input  [15:0] entradaDados,
  input  Clock,
  input  Resetar
);

  wire decoder_1_out0, decoder_1_out1, decoder_1_out2, decoder_1_out3, not_1_out, or_1_out, xor_1_out,
       xor_2_out, xor_3_out;
  wire [2:0] TAG_dout;

  D_Flip_Flop d_ff_1 (.clk(Clock), .reset(Clock));  // open: D, Q, Qn, preset
  D_Flip_Flop d_ff_2 (.clk(Clock), .reset(Clock));  // open: D, Q, Qn, preset
  D_Flip_Flop d_ff_3 (.clk(Clock), .reset(Clock));  // open: D, Q, Qn, preset
  D_Flip_Flop d_ff_4 (.clk(Clock), .reset(Clock));  // open: D, Q, Qn, preset
  Decoder #(.select(2)) decoder_1 (
    .out0(decoder_1_out0), .out1(decoder_1_out1), .out2(decoder_1_out2), .out3(decoder_1_out3),
    .sel(Endereco[2:1]));  // open: en
  LED l0 (.in(decoder_1_out0));
  LED l1 (.in(decoder_1_out1));
  LED l2 (.in(decoder_1_out2));
  LED l3 (.in(decoder_1_out3));
  RAM #(.addrWidth(2), .dataWidth(3)) TAG (.addr(Endereco[2:1]), .dout(TAG_dout));  // open: we, oe, clk, din
  RAM #(.addrWidth(2), .dataWidth(16)) Dados (.addr(Endereco[2:1]), .din(entradaDados));  // open: we, oe, clk, dout
  RAM #(.addrWidth(2), .dataWidth(1)) BitValido ();  // open: addr, we, oe, clk, din, dout
  xor xor_1 (xor_1_out, Endereco[3], TAG_dout[0]);
  xor xor_2 (xor_2_out, Endereco[4], TAG_dout[1]);
  xor xor_3 (xor_3_out, Endereco[5], TAG_dout[2]);
  or or_1 (or_1_out, xor_1_out, xor_2_out, xor_3_out);
  not not_1 (not_1_out, or_1_out);

  assign Resetar = Clock;

  // Notes on the sheet:
  //   0 - offset
  //   2-1 indice 
  //   5-3 tag
  //   bits validos 0 - 3
  //   TAG enderecamento
  //   T0 - T2
  //   TAG da linha acessada
  //   S0 - S2
  //   iguais
endmodule
